# Fritzing sketch schematic-(Fritzing-save-file) (saved by Fritzing 0.9.3b)

parts:
  Part1 = Arduino Uno (Rev3)
  Grove1 = Grove OLED 128x96

nets:
  N1: Part1.A4/SDA, Grove1.SDA
  N2: Part1.A5/SCL, Grove1.SCL
  3V3: Part1.3V3, Grove1.VCC
  GND: Part1.GND, Grove1.GND
